// Digital circuit min_term.dig as structural Verilog
module min_term (
  input  A,
  input  B,
  input  C,
  output Y1,
  output Y2,
  output Y3
);

  wire nand_1_out, or_1_out;

  or or_1 (or_1_out, A, B);
  nand nand_1 (nand_1_out, A, C);
  and and_1 (Y3, A, C);
  and and_2 (Y1, or_1_out, nand_1_out);

  assign Y2 = A;
endmodule
