// Digital circuit XOR3_new.dig as structural Verilog
module XOR3_new (
  input  A,
  input  B,
  input  C,
  output Y
);

  wire and_1_out, and_2_out, and_3_out, and_4_out, not_1_out, not_2_out, not_3_out, or_1_out, or_2_out,
       or_3_out;

  and and_1 (and_1_out, C, B, A);
  or or_1 (or_1_out, B, C);
  or or_2 (or_2_out, A, C);
  or or_3 (or_3_out, A, B);
  not not_1 (not_1_out, or_1_out);
  not not_2 (not_2_out, or_2_out);
  not not_3 (not_3_out, or_3_out);
  and and_2 (and_2_out, A, not_1_out);
  and and_3 (and_3_out, B, not_2_out);
  and and_4 (and_4_out, C, not_3_out);
  or or_4 (Y, and_1_out, and_2_out, and_3_out, and_4_out);
endmodule
