// Digital circuit kmap2-{1,2,3}.dig as structural Verilog
module kmap2__1_2_3 (
  input  A,
  input  B,
  input  C,
  input  D,
  input  E,
  output Y3,
  output Y1,
  output Y2
);

  wire and_1_out, and_2_out, and_3_out, and_4_out, and_5_out, not_1_out, not_2_out, not_3_out, not_4_out,
       not_5_out;

  not not_1 (not_1_out, A);
  not not_2 (not_2_out, B);
  not not_3 (not_3_out, C);
  not not_4 (not_4_out, D);
  not not_5 (not_5_out, E);
  or or_1 (Y1, not_2_out, C);
  and and_1 (and_1_out, A, D);
  and and_2 (and_2_out, not_3_out, D);
  and and_3 (and_3_out, not_1_out, B, not_3_out, D);
  and and_4 (and_4_out, A, B, C, D);
  and and_5 (and_5_out, B, not_4_out, E);
  or or_2 (Y2, and_1_out, B, and_2_out);
  or or_3 (Y3, and_3_out, and_4_out, and_5_out);
endmodule
