// Digital circuit kmap3.dig as structural Verilog
module kmap3 (
  input  A,
  input  B,
  input  C,
  output kmap3
);

  wire not_1_out, not_2_out, not_3_out;

  not not_1 (not_1_out, A);
  not not_2 (not_2_out, B);
  not not_3 (not_3_out, C);

  assign kmap3 = A;
endmodule
