// Digital circuit SR-latch.dig as structural Verilog
module SR_latch (
  input  R,
  input  S,
  output Q,
  output Q_2
);

  nor nor_1 (Q, R, Q_2);
  nor nor_2 (Q_2, Q, S);
endmodule

/* Test case:
R S Q ¬Q
1 0 0 1
0 0 0 1
0 1 1 0
0 0 1 0
1 0 0 1
0 0 0 1
1 0 0 1
0 0 0 1
0 1 1 0
0 0 1 0
0 1 1 0
0 0 1 0
1 1 0 0
*/
