// Digital circuit D-latch.dig as structural Verilog
module D_latch (
  input  CLK,
  input  D,
  output Q,
  output Q_2
);

  wire and_1_out, and_2_out;

  and and_1 (and_1_out, CLK, ~D);  // And
  and and_2 (and_2_out, CLK, D);
  nor nor_1 (Q, and_1_out, Q_2);
  nor nor_2 (Q_2, Q, and_2_out);
endmodule

/* Test case:
D CLK Q ¬Q
0  1  x x
0  0  x x
0  1  x x
1  1  x x
0  1  x x
0  0  x x
1  0  x x
0  0  x x
1  0  x x
1  1  x x
1  0  x x
0  0  x x
0  1  x x
0  0  x x
*/
