// Digital circuit ripple_carry_adder_4.dig as structural Verilog
module ripple_carry_adder_4 (
  input  [3:0] A,
  input  [3:0] B,
  input  C,
  output [3:0] S,
  output C_2
);

  wire add_1_c_o, add_2_c_o, add_3_c_o;

  Add add_1 (.a(A[0]), .b(B[0]), .c_i(C), .s(S[0]), .c_o(add_1_c_o));
  Add add_2 (.a(A[1]), .b(B[1]), .c_i(add_1_c_o), .s(S[1]), .c_o(add_2_c_o));
  Add add_3 (.a(A[2]), .b(B[2]), .c_i(add_2_c_o), .s(S[2]), .c_o(add_3_c_o));
  Add add_4 (.a(A[3]), .b(B[3]), .c_i(add_3_c_o), .s(S[3]), .c_o(C_2));
endmodule
