// Digital circuit XOR_new.dig as structural Verilog
module XOR_new (
  input  A,
  input  B,
  output Y
);

  wire and_1_out, not_1_out, or_1_out;

  or or_1 (or_1_out, A, B);
  and and_1 (and_1_out, A, B);
  not not_1 (not_1_out, and_1_out);
  and and_2 (Y, or_1_out, not_1_out);
endmodule
