// Digital circuit bubble3.dig as structural Verilog
module bubble3 (
  input  C,
  input  B,
  input  A,
  input  D,
  input  E,
  output Y
);

  wire and_1_out;

  and and_1 (and_1_out, A, C);  // And open: In_2
  or or_1 (Y, and_1_out, E);  // Or open: In_2
endmodule
