// Digital circuit D-Latch_vs_D-Flipflop.dig as structural Verilog
module D_Latch_vs_D_Flipflop (
  input  CLK,
  input  D,
  output Q_Flipflop,
  output Q_Latch
);

  wire and_1_out, and_2_out, and_3_out, and_4_out, and_5_out, and_6_out, nor_2_out, nor_3_out, nor_4_out,
       nor_6_out;

  and and_1 (and_1_out, ~D, CLK);  // And
  and and_2 (and_2_out, D, CLK);
  and and_3 (and_3_out, ~D, ~CLK);  // And
  and and_4 (and_4_out, D, ~CLK);  // And
  nor nor_1 (Q_Latch, and_1_out, nor_2_out);
  nor nor_2 (nor_2_out, Q_Latch, and_2_out);
  nor nor_3 (nor_3_out, and_3_out, nor_4_out);
  nor nor_4 (nor_4_out, nor_3_out, and_4_out);
  and and_5 (and_5_out, ~nor_3_out, CLK);  // And
  and and_6 (and_6_out, nor_3_out, CLK);
  nor nor_5 (Q_Flipflop, and_5_out, nor_6_out);
  nor nor_6 (nor_6_out, Q_Flipflop, and_6_out);
endmodule

/* Test case:
D CLK Q_Latch Q_Flipflop
0  1      x        x
1  1      x        x
1  0      x        x
1  1      x        x
0  1      x        x
1  1      x        x
1  0      x        x
0  0      x        x
1  0      x        x
1  1      x        x
*/
