// Digital circuit fair_coffee_machine.dig as structural Verilog
module fair_coffee_machine (
  input  clk
);

  wire A__Coin_out, and_1_out, and_2_out, and_3_out, and_4_out, and_5_out, and_6_out, and_7_out, and_8_out,
       and_9_out, and_10_out, B_1__Coffee_small_out, B_2__Coffee_large_out, or_1_out, or_2_out, or_3_out,
       or_4_out, State1_q, State2_q;

  Button A__Coin (.out(A__Coin_out));
  Button B_1__Coffee_small (.out(B_1__Coffee_small_out));
  Button B_2__Coffee_large (.out(B_2__Coffee_large_out));
  and and_1 (and_1_out, ~State1_q, ~State2_q, A__Coin_out);  // And
  and and_2 (and_2_out, ~State1_q, State2_q, ~A__Coin_out, ~B_1__Coffee_small_out);  // And
  and and_3 (and_3_out, State1_q, ~State2_q, ~A__Coin_out, B_1__Coffee_small_out, ~B_2__Coffee_large_out);  // And
  and and_4 (and_4_out, ~State1_q, State2_q, A__Coin_out);  // And
  and and_5 (and_5_out, State1_q, ~State2_q, ~A__Coin_out, ~B_1__Coffee_small_out, ~B_2__Coffee_large_out);  // And
  and and_6 (and_6_out, State1_q, ~State2_q, A__Coin_out);  // And
  or or_1 (or_1_out, and_1_out, and_2_out, and_3_out);
  or or_2 (or_2_out, and_4_out, and_5_out, and_6_out);
  D_FF State2 (.D(or_1_out), .C(clk), .Q(State2_q));  // open: nQ
  D_FF State1 (.D(or_2_out), .C(clk), .Q(State1_q));  // open: nQ
  or or_3 (or_3_out, State1_q, State2_q);
  and and_7 (and_7_out, State1_q, ~State2_q, A__Coin_out);  // And
  LED Y_1__Ready (.in(or_3_out));
  LED Y_2__Return_Coin (.in(and_7_out));
  or or_4 (or_4_out, and_8_out, and_9_out);
  and and_8 (and_8_out, ~State1_q, State2_q, B_1__Coffee_small_out);  // And
  LED Y_3__Brew_Coffee_small (.in(or_4_out));
  LED Y_4__Brew_Coffee_large (.in(and_10_out));
  and and_9 (and_9_out, State1_q, ~State2_q, B_1__Coffee_small_out);  // And
  and and_10 (and_10_out, State1_q, ~State2_q, B_2__Coffee_large_out);  // And
endmodule
