// Digital circuit fancy_coffee_machine.dig as structural Verilog
module fancy_coffee_machine (
  input  clk
);

  wire A__Coin_out, and_1_out, and_2_out, and_3_out, and_4_out, and_5_out, and_6_out, and_7_out, and_8_out,
       and_9_out, and_10_out, and_11_out, and_12_out, and_13_out, and_14_out, and_15_out, and_16_out,
       and_17_out, B_1__Coffee_small_out, B_2__Coffee_large_out, B_3__Latte_Macchiato_out, or_1_out,
       or_2_out, or_3_out, or_4_out, or_5_out, or_6_out, State1_q, State2_q;

  Button A__Coin (.out(A__Coin_out));
  Button B_1__Coffee_small (.out(B_1__Coffee_small_out));
  Button B_2__Coffee_large (.out(B_2__Coffee_large_out));
  Button B_3__Latte_Macchiato (.out(B_3__Latte_Macchiato_out));
  and and_1 (and_1_out, ~State1_q, ~State2_q, A__Coin_out);  // And
  and and_2 (and_2_out, ~State1_q, State2_q, ~A__Coin_out, ~B_1__Coffee_small_out);  // And
  and and_3 (and_3_out, State1_q, ~State2_q, ~A__Coin_out, B_1__Coffee_small_out, ~B_2__Coffee_large_out);  // And
  and and_4 (and_4_out, State1_q, State2_q, ~A__Coin_out, B_2__Coffee_large_out, ~B_3__Latte_Macchiato_out);  // And
  and and_5 (and_5_out, State1_q, ~State2_q, A__Coin_out);  // And
  and and_6 (and_6_out, State1_q, State2_q, ~A__Coin_out, ~B_1__Coffee_small_out, ~B_2__Coffee_large_out, ~B_3__Latte_Macchiato_out);  // And
  and and_7 (and_7_out, State1_q, State2_q, A__Coin_out);
  and and_8 (and_8_out, ~State1_q, State2_q, A__Coin_out);  // And
  and and_9 (and_9_out, State1_q, ~State2_q, ~A__Coin_out, ~B_1__Coffee_small_out, ~B_2__Coffee_large_out);  // And
  and and_10 (and_10_out, State1_q, State2_q, ~A__Coin_out, B_1__Coffee_small_out, ~B_2__Coffee_large_out, ~B_3__Latte_Macchiato_out);  // And
  or or_1 (or_1_out, and_5_out, and_6_out, and_7_out);
  or or_2 (or_2_out, and_1_out, and_2_out, and_3_out, and_4_out, or_1_out);
  or or_3 (or_3_out, or_1_out, and_8_out, and_9_out, and_10_out);
  or or_4 (or_4_out, State1_q, State2_q);
  D_FF State2 (.D(or_2_out), .C(clk), .Q(State2_q));  // open: nQ
  D_FF State1 (.D(or_3_out), .C(clk), .Q(State1_q));  // open: nQ
  and and_11 (and_11_out, State1_q, State2_q, A__Coin_out);
  and and_12 (and_12_out, ~State1_q, State2_q, ~A__Coin_out, B_1__Coffee_small_out);  // And
  LED Y_1__Ready (.in(or_4_out));
  LED Y_2__Return_Coin (.in(and_11_out));
  or or_5 (or_5_out, and_12_out, and_13_out, and_14_out);
  and and_13 (and_13_out, State1_q, ~State2_q, ~A__Coin_out, B_1__Coffee_small_out, ~B_2__Coffee_large_out);  // And
  LED Y_3__Brew_Coffee_small (.in(or_5_out));
  LED Y_4__Brew_Coffee_large (.in(or_6_out));
  LED Y_5__Brew_Latte_Macchiato (.in(and_17_out));
  and and_14 (and_14_out, State1_q, State2_q, ~A__Coin_out, B_1__Coffee_small_out, ~B_2__Coffee_large_out, ~B_3__Latte_Macchiato_out);  // And
  and and_15 (and_15_out, State1_q, ~State2_q, ~A__Coin_out, B_2__Coffee_large_out);  // And
  or or_6 (or_6_out, and_15_out, and_16_out);
  and and_16 (and_16_out, State1_q, State2_q, ~A__Coin_out, B_2__Coffee_large_out, ~B_3__Latte_Macchiato_out);  // And
  and and_17 (and_17_out, State1_q, State2_q, ~A__Coin_out, B_3__Latte_Macchiato_out);  // And
endmodule
